// Logisim project 4bitCpu.circ as structural Verilog: 1 circuit, main circuit main
module main (
);

  wire Add, and_1_out, and_2_out, and_3_out, button_1_out, button_2_out, button_3_out, button_4_out, C0, C1,
       C2, C3, C4, C5, C6, C7, C8, C9, C10, C11, C12, C13, C14, C15, ChangeRomSec, CheckInput, ChngeVrminput,
       CL, comparator_1_eq, controlled_buffer_1_out, controlled_buffer_8_out, controlled_buffer_9_out,
       controlled_buffer_10_out, controlled_buffer_11_out, decoder_2_out0, decoder_4_out0, decoder_4_out1,
       decoder_4_out2, decoder_4_out3, DisplyEnble, GPUclock, Increment, JMP, JMPifA0, LDI, LoadRamBank,
       LoadRamIntoAFromAdrr, LodCoordintes, MOV, multiplexer_2_out, or_1_out, or_2_out, register_3_q,
       register_4_q, register_5_q, Sub, t_ff_1_q, undriven_2, VRam_dout, writeAintoRamAtAdrr, WriteVRam,
       WriteX, WriteY;
  wire [1:0] counter_1_q;
  wire [3:0] Addout, bit_extender_1_out, controlled_buffer_2_out, InputOut, Operand, outA, outB, RamBankAdr,
       RamOut, register_1_q, register_2_q, RomSec, SubOut;
  wire [7:0] counter_2_q, counter_3_q, multiplexer_1_out, rom_1_data, undriven;
  wire [7:4] register_6_q;
  wire [15:0] controlled_buffer_7_out, Row0out, Row1out, Row2out, Row3out, Row4out, Row5out, Row6out,
       Row7out, Row8out, Row9out, Row10out, Row11out, Row12out, Row13out, Row14out, Row15out;

  and and_1 (and_1_out, GPUclock, LodCoordintes);
  and and_2 (and_2_out, GPUclock, LodCoordintes);
  Comparator #(.width(4)) comparator_1 (.a(outA), .b(4'b0000), .eq(comparator_1_eq));  // open: gt, lt
  Counter #(.max('h3), .width(2)) counter_1 (
    .up(1'b1), .clk(GPUclock), .Q(counter_1_q));  // open: clr, load, count, D, carry
  Register #(.width(4)) register_1 (.D(outA), .en(WriteX), .clk(and_1_out), .Q(register_1_q));  // open: clr
  Register #(.width(4)) register_2 (.D(outA), .en(WriteY), .clk(and_2_out), .Q(register_2_q));  // open: clr
  and and_3 (and_3_out, JMPifA0, comparator_1_eq);
  or or_1 (or_1_out, and_3_out, JMP);
  Clock #(.highDuration(5), .lowDuration(5)) clock_1 (.out(CL));
  Decoder #(.select(2)) decoder_1 (
    .out0(LodCoordintes), .out2(DisplyEnble), .out3(Increment), .sel(counter_1_q));  // open: out1, en
  Clock clock_2 (.out(GPUclock));
  Counter counter_2 (
    .clr(1'b0), .load(or_1_out), .up(1'b1), .clk(CL), .D({RomSec, Operand}), .Q(counter_2_q));  // open: count, carry
  Counter counter_3 (
    .up(1'b1), .clk(controlled_buffer_1_out), .D(undriven), .Q(counter_3_q));  // open: clr, load, count, carry
  assign controlled_buffer_1_out = Increment ? GPUclock : 1'bz;  // Controlled_Buffer controlled_buffer_1
  Register #(.width(1)) register_3 (.D(WriteVRam), .en(1'b1), .clk(GPUclock), .Q(register_3_q), .clr(undriven_2));
  Register #(.width(1)) register_4 (.D(LoadRamIntoAFromAdrr), .en(1'b1), .clk(CL), .Q(register_4_q));  // open: clr
  Register #(.width(1)) register_5 (.D(CheckInput), .en(1'b1), .clk(CL), .Q(register_5_q));  // open: clr
  RAM #(.dataWidth(4)) GeneralRam (
    .addr({Operand, RamBankAdr}), .we(writeAintoRamAtAdrr), .oe(LoadRamIntoAFromAdrr), .clk(CL), .din(outA),
    .dout(RamOut));
  ROM rom_1 (.addr(counter_2_q), .data(rom_1_data));
  Multiplexer #(.width(8)) multiplexer_1 (
    .in0(counter_3_q), .in1({register_2_q, register_1_q}), .out(multiplexer_1_out), .sel(WriteVRam));
  T_Flip_Flop t_ff_1 (.T(1'b1), .clk(ChngeVrminput), .Q(t_ff_1_q));  // open: Qn, reset, preset
  assign controlled_buffer_2_out = register_5_q ? InputOut : 4'bz;  // Controlled_Buffer controlled_buffer_2
  assign controlled_buffer_2_out = Add ? Addout : 4'bz;  // Controlled_Buffer controlled_buffer_3
  assign controlled_buffer_2_out = Sub ? SubOut : 4'bz;  // Controlled_Buffer controlled_buffer_4
  assign controlled_buffer_2_out = register_4_q ? RamOut : 4'bz;  // Controlled_Buffer controlled_buffer_5
  assign controlled_buffer_2_out = LDI ? Operand : 4'bz;  // Controlled_Buffer controlled_buffer_6
  RAM #(.dataWidth(1)) VRam (
    .addr(multiplexer_1_out), .we(register_3_q), .clk(GPUclock), .din(t_ff_1_q), .dout(VRam_dout));  // open: oe
  or or_2 (or_2_out, Add, Sub, register_5_q, register_4_q, LDI);
  Register register_6 (.D(rom_1_data), .en(1'b1), .clk(CL), .Q({register_6_q, Operand}), .clr(1'b0));
  Register #(.width(4)) B (.D(outA), .en(MOV), .clk(CL), .Q(outB));  // open: clr
  Register #(.width(4)) A (.D(controlled_buffer_2_out), .en(or_2_out), .clk(CL), .Q(outA));  // open: clr
  Register #(.width(4)) RamBankAdress (.D(Operand), .en(LoadRamBank), .clk(CL), .Q(RamBankAdr));  // open: clr
  Register #(.width(4)) u_RomSec (.D(Operand), .en(ChangeRomSec), .clk(CL), .Q(RomSec));  // open: clr
  LED led_1 (.in(decoder_2_out0));
  Decoder #(.select(4)) decoder_2 (
    .out0(decoder_2_out0), .out1(LDI), .out2(Add), .out3(Sub), .out4(MOV), .out5(CheckInput), .out6(JMP),
    .out7(JMPifA0), .out8(ChangeRomSec), .out9(LoadRamBank), .out10(writeAintoRamAtAdrr),
    .out11(LoadRamIntoAFromAdrr), .out12(WriteVRam), .out13(WriteY), .out14(WriteX), .out15(ChngeVrminput),
    .sel(register_6_q), .en(1'b1));
  assign controlled_buffer_7_out = VRam_dout ? {C15, C14, C13, C12, C11, C10, C9, C8, C7, C6, C5, C4, C3, C2, C1, C0} : 16'bz;  // Controlled_Buffer controlled_buffer_7
  Decoder #(.select(4)) decoder_3 (
    .out0(C15), .out1(C14), .out2(C13), .out3(C12), .out4(C11), .out5(C10), .out6(C9), .out7(C8), .out8(C7),
    .out9(C6), .out10(C5), .out11(C4), .out12(C3), .out13(C2), .out14(C1), .out15(C0),
    .sel(counter_3_q[3:0]), .en(DisplyEnble));
  Adder #(.width(4)) adder_1 (.a(outA), .b(outB), .out(Addout));  // open: cin, cout
  Subtractor #(.width(4)) subtractor_1 (.a(outA), .b(outB), .out(SubOut));  // open: bin, bout
  Demultiplexer #(.select(4), .width(16)) demultiplexer_1 (
    .out0(Row0out), .out1(Row1out), .out2(Row2out), .out3(Row3out), .out4(Row4out), .out5(Row5out),
    .out6(Row6out), .out7(Row7out), .out8(Row8out), .out9(Row9out), .out10(Row10out), .out11(Row11out),
    .out12(Row12out), .out13(Row13out), .out14(Row14out), .out15(Row15out), .in(controlled_buffer_7_out),
    .sel(counter_3_q[7:4]));
  Decoder #(.select(2)) decoder_4 (
    .out0(decoder_4_out0), .out1(decoder_4_out1), .out2(decoder_4_out2), .out3(decoder_4_out3),
    .sel(Operand[1:0]));  // open: en
  Button button_1 (.out(button_1_out));
  Button button_2 (.out(button_2_out));
  Button button_3 (.out(button_3_out));
  assign controlled_buffer_8_out = decoder_4_out2 ? button_2_out : 1'bz;  // Controlled_Buffer controlled_buffer_8
  assign controlled_buffer_9_out = decoder_4_out3 ? button_1_out : 1'bz;  // Controlled_Buffer controlled_buffer_9
  Button button_4 (.out(button_4_out));
  Button button_5 ();  // open: out
  assign controlled_buffer_10_out = decoder_4_out0 ? button_3_out : 1'bz;  // Controlled_Buffer controlled_buffer_10
  assign controlled_buffer_11_out = decoder_4_out1 ? button_4_out : 1'bz;  // Controlled_Buffer controlled_buffer_11
  Multiplexer #(.select(2)) multiplexer_2 (
    .in0(controlled_buffer_10_out), .in1(controlled_buffer_11_out), .in2(controlled_buffer_8_out),
    .in3(controlled_buffer_9_out), .out(multiplexer_2_out), .sel(Operand[1:0]));
  assign bit_extender_1_out = {{3{1'b0}}, multiplexer_2_out};  // Bit_Extender bit_extender_1
  Register #(.width(4)) register_7 (.D(bit_extender_1_out), .en(CheckInput), .clk(CL), .Q(InputOut));  // open: clr
  DotMatrix #(.inputtype("row"), .matrixcols(16), .matrixrows(16), .persist(2048)) dotmatrix_1 (
    .row0(Row0out), .row1(Row1out), .row2(Row2out), .row3(Row3out), .row4(Row4out), .row5(Row5out),
    .row6(Row6out), .row7(Row7out), .row8(Row8out), .row9(Row9out), .row10(Row10out), .row11(Row11out),
    .row12(Row12out), .row13(Row13out), .row14(Row14out), .row15(Row15out));

  // Notes on the sheet:
  //   contents of rom_1 (hex, n*v repeats v):
  //   11 40 13 20 a0
  //   Opcode
  //   1x
  //   2
  //   3
  //   0
  //   Input
  //   On/Off
  //   1
endmodule
